# Fritzing sketch Leak Sensor Device (saved by Fritzing 0.9.4)
circuit board: 5.0714cm x 2.31923cm
perfboards: 1

parts:
  Part1 = Adafruit Feather HUZZAH ESP8266 [part_number="Adafruit #2821"]
  D2 = Diode [package=diode-1n4001]
  D1 = Diode [package=diode-1n4001]
  JP1 = M16 [package=1x16_machine-pin-header_lock.004]
  JP2 = Header 12 [package=1x12_machine-pin-header_lock.004]
  R1 = Resistor [tolerance=±5% resistance=220 package=THT]

nets:
  N1: Part1.CH_PD, JP1.16
  N2: Part1.TXD, JP1.15
  N3: Part1.RXD, JP1.14
  N4: Part1.GPIO12/MISO, D2.A, JP1.13, JP2.5
  N5: Part1.GPIO13/MOSI, JP1.12, JP2.6
  N6: Part1.GPIO14/SCK, JP1.11, JP2.4
  N7: Part1.ADC, JP1.5
  N8: Part1.GND, JP1.4
  N9: Part1.3.3V, JP1.2, R1.Pin_0
  N10: Part1.RESET, JP1.1
  N11: Part1.VBAT, JP2.1
  N12: Part1.EN, JP2.2
  N13: Part1.VBUS, JP2.3
  N14: Part1.GPIO15, JP2.7
  N15: Part1.GPIO0, JP2.8
  N16: Part1.GPIO16, JP2.9
  N17: Part1.GPIO2, JP2.10
  N18: Part1.GPIO5/SCL, JP2.11
  N19: Part1.GPIO4/SDA, D1.A, JP2.12
  N20: D2.C, D1.C, R1.Pin_1

notes:
  Connect Leak Sensor 1 between GPIO4 and GND
  Connect Leak Sensor 2 between GPIO12 and GND

custom parts:
  Adafruit Feather HUZZAH ESP8266: his is the Adafruit Feather HUZZAH ESP8266 - our take on an 'all-in-one' ESP8266 WiFi development board with built in USB and battery charging. Its an ESP8266 WiFi module with all the extras you need, ready to rock! We have other boards in the Feather family, check'em out here. At the Feather HUZZAH's heart is an ESP8266 WiFi microcontroller clocked at 80 MHz and at 3.3V logic. This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
